# Fritzing sketch sketch-lolin32 (saved by Fritzing 0.9.3b)
stripboards: 1

parts:
  U1 = lolin
  temp_inside = DS18B20 1-Wire Temperature Sensor [part_number=DS18B20]
  temp_outside = DS18B20 1-Wire Temperature Sensor [part_number=DS18B20]  # not connected
  Sunlight = BH1750
  soil0 = FC-28 Soil Hygrometer Module
  soil1 = FC-28 Soil Hygrometer Module
  soil2 = FC-28 Soil Hygrometer Module
  rain0 = FC-28 Soil Hygrometer Module
  Part1 = FC-28 Soil Hygrometer Module - Probe
  Part2 = FC-28 Soil Hygrometer Module - Probe
  Part3 = FC-28 Soil Hygrometer Module - Probe
  YL-83_-_Detection_Board1 = YL-83 Rain Sensor - Detection Board
  U2 = 7-SEGMENT-4DIGIT [package=7-segment-4digit-youngsun]
  S1 = Toggle Switch [package=THT]  # not connected
  J1 = female pin header, 4 pins [form="♀ (female)"]

nets:
  N1: U1.connector4, soil0.AO
  N2: U1.connector5, soil1.AO
  N3: U1.connector6, soil2.AO
  N4: U1.connector7, rain0.AO
  N5: U1.connector20, rain0.GND
  VCC: U1.connector25, soil2.VCC, rain0.VCC
  N6: U1.connector28, U2.5, J1.pin3
  N7: U1.connector29, U2.3, J1.pin2
  N8: U1.connector30, soil2.GND
  N9: U1.connector32, Sunlight.SDA
  N10: U1.connector33, Sunlight.SCL
  VCC_2: U1.connector34, soil0.VCC, soil1.VCC
  GND: U1.connector37, temp_inside.GND, soil0.GND, soil1.GND, U2.1, J1.pin1
  N11: Sunlight.VCC, U2.7, J1.pin4
  N12: soil0.POS, Part1.POS
  N13: soil0.NEG, Part1.NEG
  N14: soil1.POS, Part2.POS
  N15: soil1.NEG, Part2.NEG
  N16: soil2.POS, Part3.POS
  N17: soil2.NEG, Part3.NEG
  N18: rain0.POS, YL-83_-_Detection_Board1.POS
  N19: rain0.NEG, YL-83_-_Detection_Board1.NEG

notes:
  SOIL-0: 32
  SOIL-1: 33
  SOIL-2: 34
  RAIN-0: 35
  LIGHT
  SDA: 21
  SCL: 22
  TEMP: 18
  DISPLAY
  DIO: 23
  CLK: 19
  LOLIN32

custom parts:
  BH1750: Light Sensor
  FC-28 Soil Hygrometer Module: The FC-28 is a soil hygrometer module that uses the Texas Instruments LM393 comparator chip to provide an analog measurement of soil humidity. The digital output is high when soil moisture is over a certain threshold, as determined by adjusting the potentiometer.
  FC-28 Soil Hygrometer Module - Probe: The FC-28 is a soil hygrometer module that uses the Texas Instruments LM393 comparator chip to provide an analog measurement of soil humidity.
  YL-83 Rain Sensor - Detection Board: The YL-83 is a rain sensor that has more resistance when dry and less resistance when wet. The module runs at 5V.
